// Logisim project trabalho_todo.circ as structural Verilog
module Banco_de_Registradores (
  input  [31:0] WRITE,
  input  [3:0] RD,
  input  WR,
  input  [3:0] RS1_I,
  input  [3:0] RS2_I,
  input  CLK,
  output [31:0] RS1_O,
  output [31:0] RS2_O
);

  wire demultiplexer_1_out0, demultiplexer_1_out1, demultiplexer_1_out2, demultiplexer_1_out3,
       demultiplexer_1_out4, demultiplexer_1_out5, demultiplexer_1_out6, demultiplexer_1_out7,
       demultiplexer_1_out8, demultiplexer_1_out9, demultiplexer_1_out10, demultiplexer_1_out11,
       demultiplexer_1_out12, demultiplexer_1_out13, demultiplexer_1_out14, demultiplexer_1_out15;
  wire [31:0] X0_q, X1_q, X2_q, X3_q, X4_q, X5_q, X6_q, X7_q, X8_q, X9_q, X10_q, X11_q, X12_q, X13_q, X14_q,
       X15_q;

  Demultiplexer #(.select(4)) demultiplexer_1 (
    .out0(demultiplexer_1_out0), .out1(demultiplexer_1_out1), .out2(demultiplexer_1_out2),
    .out3(demultiplexer_1_out3), .out4(demultiplexer_1_out4), .out5(demultiplexer_1_out5),
    .out6(demultiplexer_1_out6), .out7(demultiplexer_1_out7), .out8(demultiplexer_1_out8),
    .out9(demultiplexer_1_out9), .out10(demultiplexer_1_out10), .out11(demultiplexer_1_out11),
    .out12(demultiplexer_1_out12), .out13(demultiplexer_1_out13), .out14(demultiplexer_1_out14),
    .out15(demultiplexer_1_out15), .in(WR), .sel(RD));
  Register #(.width(32)) X0 (.D(WRITE), .en(demultiplexer_1_out11), .clk(CLK), .Q(X0_q));  // open: clr
  Register #(.width(32)) X1 (.D(WRITE), .en(demultiplexer_1_out10), .clk(CLK), .Q(X1_q));  // open: clr
  Register #(.width(32)) X2 (.D(WRITE), .en(demultiplexer_1_out9), .clk(CLK), .Q(X2_q));  // open: clr
  Register #(.width(32)) X3 (.D(WRITE), .en(demultiplexer_1_out8), .clk(CLK), .Q(X3_q));  // open: clr
  Register #(.width(32)) X4 (.D(WRITE), .en(demultiplexer_1_out7), .clk(CLK), .Q(X4_q));  // open: clr
  Register #(.width(32)) X5 (.D(WRITE), .en(demultiplexer_1_out6), .clk(CLK), .Q(X5_q));  // open: clr
  Register #(.width(32)) X6 (.D(WRITE), .en(demultiplexer_1_out5), .clk(CLK), .Q(X6_q));  // open: clr
  Register #(.width(32)) X7 (.D(WRITE), .en(demultiplexer_1_out4), .clk(CLK), .Q(X7_q));  // open: clr
  Register #(.width(32)) X8 (.D(WRITE), .en(demultiplexer_1_out3), .clk(CLK), .Q(X8_q));  // open: clr
  Register #(.width(32)) X9 (.D(WRITE), .en(demultiplexer_1_out2), .clk(CLK), .Q(X9_q));  // open: clr
  Register #(.width(32)) X10 (.D(WRITE), .en(demultiplexer_1_out1), .clk(CLK), .Q(X10_q));  // open: clr
  Register #(.width(32)) X11 (.D(WRITE), .en(demultiplexer_1_out0), .clk(CLK), .Q(X11_q));  // open: clr
  Register #(.width(32)) X12 (.D(WRITE), .en(demultiplexer_1_out12), .clk(CLK), .Q(X12_q));  // open: clr
  Register #(.width(32)) X13 (.D(WRITE), .en(demultiplexer_1_out13), .clk(CLK), .Q(X13_q));  // open: clr
  Register #(.width(32)) X14 (.D(WRITE), .en(demultiplexer_1_out14), .clk(CLK), .Q(X14_q));  // open: clr
  Register #(.width(32)) X15 (.D(WRITE), .en(demultiplexer_1_out15), .clk(CLK), .Q(X15_q));  // open: clr
  Multiplexer #(.select(4), .width(32)) multiplexer_1 (
    .in0(X15_q), .in1(X14_q), .in2(X13_q), .in3(X12_q), .in4(X11_q), .in5(X10_q), .in6(X9_q), .in7(X8_q),
    .in8(X0_q), .in9(X1_q), .in10(X2_q), .in11(X3_q), .in12(X4_q), .in13(X5_q), .in14(X6_q), .in15(X7_q),
    .out(RS1_O), .sel(RS1_I));
  Multiplexer #(.select(4), .width(32)) multiplexer_2 (
    .in0(X0_q), .in1(X1_q), .in2(X2_q), .in3(X3_q), .in4(X4_q), .in5(X5_q), .in6(X6_q), .in7(X7_q),
    .in8(X8_q), .in9(X9_q), .in10(X10_q), .in11(X11_q), .in12(X12_q), .in13(X13_q), .in14(X14_q),
    .in15(X15_q), .out(RS2_O), .sel(RS2_I));
endmodule

module main (
);

  wire and_1_out, branch_1_is_branch, branch_1_o_branch, CLK, MR, MU_IMM, MU_ULA, RS2_or_RD, WM, WR;
  wire [1:0] MU_PC, OP_B;
  wire [3:0] multiplexer_1_out;
  wire [23:0] rom_1_data;
  wire [31:0] adder_1_out, adder_2_out, adder_3_out, banco_de_registradores_1_rs1_o,
       banco_de_registradores_1_rs2_o, multiplexer_2_out, multiplexer_3_out, multiplexer_4_out,
       multiplexer_5_out, pc_1_o_pc, processador_de_imm_1_o, ram_1_dout, ula_1_ula_o;

  Clock clock_1 (.out(CLK));
  PC pc_1 (.I_PC(multiplexer_4_out), .CLK(CLK), .O_PC(pc_1_o_pc));
  ROM #(.addrWidth(24), .dataWidth(24)) rom_1 (.addr(pc_1_o_pc[23:0]), .data(rom_1_data));
  Multiplexer #(.width(4)) multiplexer_1 (
    .in0(rom_1_data[17:14]), .in1(rom_1_data[9:6]), .out(multiplexer_1_out), .sel(RS2_or_RD));
  Unidade_de_Controle unidade_de_controle_1 (
    .OPCODE(rom_1_data[2:0]), .MU_PC(MU_PC), .OP_B(OP_B), .MR(MR), .WM(WM), .WR(WR), .MU_ULA(MU_ULA),
    .MU_IMM(MU_IMM), .RS2_or_RD(RS2_or_RD));
  Processador_de_IMM processador_de_imm_1 (.I(rom_1_data), .MU_IMM(MU_IMM), .O(processador_de_imm_1_o));
  Banco_de_Registradores banco_de_registradores_1 (
    .WRITE(multiplexer_5_out), .RD(rom_1_data[9:6]), .WR(WR), .RS1_I(rom_1_data[13:10]),
    .RS2_I(multiplexer_1_out), .CLK(CLK), .RS1_O(banco_de_registradores_1_rs1_o),
    .RS2_O(banco_de_registradores_1_rs2_o));
  Adder #(.width(32)) adder_1 (.a(pc_1_o_pc), .out(adder_1_out), .cin(1'b1));  // open: b, cout
  Adder #(.width(32)) adder_2 (.a(pc_1_o_pc), .b(processador_de_imm_1_o), .out(adder_2_out));  // open: cin, cout
  Multiplexer #(.width(32)) multiplexer_2 (
    .in0(banco_de_registradores_1_rs2_o), .in1(processador_de_imm_1_o), .out(multiplexer_2_out), .sel(MU_ULA));
  ULA ula_1 (
    .RS1(banco_de_registradores_1_rs1_o), .RS2(multiplexer_2_out), .OP_ULA(rom_1_data[5:3]),
    .ULA_O(ula_1_ula_o));
  BRANCH branch_1 (
    .B_RS1(banco_de_registradores_1_rs1_o), .B_RS2(banco_de_registradores_1_rs2_o), .OP_B(OP_B),
    .O_BRANCH(branch_1_o_branch), .IS_BRANCH(branch_1_is_branch));
  Adder #(.width(32)) adder_3 (.a(ula_1_ula_o), .b(processador_de_imm_1_o), .out(adder_3_out));  // open: cin, cout
  Multiplexer #(.select(2), .width(32)) multiplexer_3 (
    .in0(adder_1_out), .in1(adder_3_out), .in3(adder_2_out), .out(multiplexer_3_out), .sel(MU_PC));  // open: in2
  RAM #(.addrWidth(24), .dataWidth(32)) ram_1 (
    .addr(ula_1_ula_o[23:0]), .we(WM), .oe(1'b1), .clk(CLK), .dout(ram_1_dout));  // open: din
  Multiplexer #(.width(32)) multiplexer_4 (
    .in0(multiplexer_3_out), .in1(adder_2_out), .out(multiplexer_4_out), .sel(and_1_out));
  and and_1 (and_1_out, branch_1_o_branch, branch_1_is_branch);
  Multiplexer #(.width(32)) multiplexer_5 (.in0(ula_1_ula_o), .in1(ram_1_dout), .out(multiplexer_5_out), .sel(MR));

  // Notes on the sheet:
  //   contents of rom_1 (hex, n*v repeats v):
  //   0 8 10 18 20 28 1 9 11 19 21 2 a 12 1a 22 3
  //   Memoria_de_Instruções
  //   PC
  //   PC + 1
  //   PC + IMM
  //   RS1 + IMM
  //   Memoria_de_Dados
endmodule

module ULA (
  input  [2:0] OP_ULA,
  input  [31:0] RS1,
  input  [31:0] RS2,
  output [31:0] ULA_O
);

  wire [31:0] adder_1_out, divider_1_out, multiplier_1_out, shifter_1_out, shifter_2_out, subtractor_1_out;

  Adder #(.width(32)) adder_1 (.a(RS2), .b(RS1), .out(adder_1_out));  // open: cin, cout
  Subtractor #(.width(32)) subtractor_1 (.a(RS2), .b(RS1), .out(subtractor_1_out));  // open: bin, bout
  Multiplier #(.width(32)) multiplier_1 (.a(RS2), .b(RS1), .out(multiplier_1_out));  // open: cin, cout
  Divider #(.width(32)) divider_1 (.a(RS2), .b(RS1), .out(divider_1_out));  // open: upper, rem
  Shifter #(.width(32)) shifter_1 (.in(RS1), .\dist (RS2[4:0]), .out(shifter_1_out));
  Shifter #(.shift("lr"), .width(32)) shifter_2 (.in(RS1), .\dist (RS2[4:0]), .out(shifter_2_out));
  Multiplexer #(.select(3), .width(32)) multiplexer_1 (
    .in0(adder_1_out), .in1(subtractor_1_out), .in2(multiplier_1_out), .in3(divider_1_out),
    .in4(shifter_1_out), .in5(shifter_2_out), .out(ULA_O), .sel(OP_ULA));  // open: in6, in7
endmodule

module Unidade_de_Controle (
  input  [2:0] OPCODE,
  output [1:0] MU_PC,
  output [1:0] OP_B,
  output MR,
  output WM,
  output WR,
  output MU_ULA,
  output MU_IMM,
  output RS2_or_RD
);

  wire [1:0] rom_1_data;

  ROM #(.addrWidth(3), .dataWidth(10)) rom_1 (
    .addr(OPCODE), .data({RS2_or_RD, OP_B[1], MU_IMM, MU_ULA, WR, WM, MR, OP_B[0], rom_1_data}));
endmodule

module Processador_de_IMM (
  input  [23:0] I,
  input  MU_IMM,
  output [31:0] O
);

  wire [31:0] bit_extender_1_out, bit_extender_2_out;

  assign bit_extender_1_out = {{22{I[23]}}, I[23:14]};  // Bit_Extender bit_extender_1
  assign bit_extender_2_out = {{15{I[23]}}, {I[23:10], I[5:3]}};  // Bit_Extender bit_extender_2
  Multiplexer #(.width(32)) multiplexer_1 (.in0(bit_extender_1_out), .in1(bit_extender_2_out), .out(O), .sel(MU_IMM));

  // Notes on the sheet:
  //   Tipo I, S, B
  //   Tipo J
endmodule

module MI (
  input  [31:0] PC,
  output [23:0] O
);

  ROM #(.addrWidth(24), .dataWidth(24)) rom_1 (.addr(PC[23:0]), .data(O));

  // Notes on the sheet:
  //   contents of rom_1 (hex, n*v repeats v):
  //   0 8 10 18 20 28 1 9 11 19 21 2 a 12 1a 22 3
endmodule

module PC (
  input  [31:0] I_PC,
  input  CLK,
  output [31:0] O_PC
);

  Register #(.width(32)) register_1 (.D(I_PC), .en(1'b1), .clk(CLK), .Q(I_PC));  // open: clr

  assign O_PC = I_PC;
endmodule

module BRANCH (
  input  [31:0] B_RS1,
  input  [31:0] B_RS2,
  input  [1:0] OP_B,
  output O_BRANCH,
  output IS_BRANCH
);

  wire comparator_1_eq, comparator_1_gt, comparator_1_lt, not_1_out, or_2_out;

  Comparator #(.width(32)) comparator_1 (
    .a(B_RS1), .b(B_RS2), .gt(comparator_1_gt), .eq(comparator_1_eq), .lt(comparator_1_lt));
  or or_1 (IS_BRANCH, comparator_1_gt, comparator_1_eq, comparator_1_lt);
  not not_1 (not_1_out, comparator_1_eq);
  or or_2 (or_2_out, comparator_1_gt, comparator_1_eq);
  Multiplexer #(.select(2)) multiplexer_1 (
    .in0(or_2_out), .in1(comparator_1_eq), .in2(not_1_out), .in3(comparator_1_lt), .out(O_BRANCH), .sel(OP_B));
endmodule
